# Fritzing sketch smart_knee_bracelet_project_schematic (saved by Fritzing 0.9.3b)
breadboards: 1

parts:
  Flex_Sensor = Basic Flex Resistor
  C1 = Ceramic Capacitor [capacitance=100nF package="100 mil [THT, multilayer]"]
  C2 = Electrolytic Capacitor [capacitance=1µF package="100 mil [THT, electrolytic]"]
  C3 = Ceramic Capacitor [capacitance=100nF package="100 mil [THT, multilayer]"]
  C4 = Electrolytic Capacitor [capacitance=1µF package="100 mil [THT, electrolytic]"]
  C5 = Ceramic Capacitor [capacitance=100nF package="100 mil [THT, multilayer]"]
  C6 = Electrolytic Capacitor [capacitance=1µF package="100 mil [THT, electrolytic]"]
  Force_Sensor_1 = Basic Force Sensing Resistor (FSR) [package=THT]
  Force_Sensor_2 = Basic Force Sensing Resistor (FSR) [package=THT]
  MicroController = Lilypad Arduino Board
  R1 = Resistor [tolerance=±5% resistance=220 package="0603 [SMD]"]
  R2 = Resistor [tolerance=±5% resistance=220 package="0603 [SMD]"]
  R3 = Resistor [tolerance=±5% resistance=220 package="0603 [SMD]"]
  J1 = Basic Servo

nets:
  N1: Flex_Sensor.pin_1, R1.Pin_0
  N2: C1.1, C2.+, MicroController.A1
  N3: C3.0, C4.+, MicroController.A0
  N4: C5.1, C6.+, MicroController.A2
  N5: Force_Sensor_1.pin_1, R2.Pin_0
  N6: Force_Sensor_2.pin_1, R3.Pin_0
  N7: MicroController.D3, J1.pulse
